// Logisim project risc-v-system.circ as structural Verilog: 10 circuits, main circuit System
module System (
);

  wire and_1_out, and_2_out, and_3_out, and_4_out, and_5_out, and_6_out, and_7_out, and_8_out, and_9_out,
       and_10_out, and_11_out, and_12_out, and_13_out, and_14_out, and_15_out, and_16_out, button_1_out,
       button_5_out, button_6_out, clock_1_out, clock_2_out, clock_3_out, clock_4_out, clock_5_out,
       clock_6_out, clock_7_out, clock_8_out, clock_9_out, comparator_1_eq, comparator_2_eq, comparator_3_eq,
       comparator_4_eq, comparator_5_eq, comparator_6_eq, comparator_8_eq, comparator_9_eq, comparator_10_eq,
       comparator_11_eq, comparator_12_eq, CPU_unsupported_instruction, d_ff_1_qn, d_ff_2_q, d_ff_3_q,
       d_ff_3_qn, d_ff_4_q, d_ff_4_qn, keyboard_1_avail, lt, MemRead, MemWrite, multiplexer_1_out,
       multiplexer_2_out, multiplexer_3_out, or_1_out, rot, rst, rt, s_r_ff_1_q;
  wire [3:0] CPU_pc_out_2, CPU_pc_out_3;
  wire [6:0] keyboard_1_data;
  wire [31:0] Address, bit_extender_1_out, bit_extender_2_out, bit_extender_3_out, bit_extender_4_out,
       bit_extender_5_out, CPU_pc_out, Data_in, Data_out, register_1_q, videoram_1__0, videoram_1__1,
       videoram_1__2, videoram_1__3, videoram_1__4, videoram_1__5, videoram_1__6, videoram_1__7,
       videoram_1__8, videoram_1__9, videoram_1__10, videoram_1__11, videoram_1__12, videoram_1__13,
       videoram_1__14, videoram_1__15, videoram_1__16, videoram_1__17, videoram_1__18, videoram_1__19,
       videoram_1__20, videoram_1__21, videoram_1__22, videoram_1__23, videoram_1__24, videoram_1__25,
       videoram_1__26, videoram_1__27, videoram_1__28, videoram_1__29, videoram_1__30, videoram_1__31;

  Hex_Digit_Display hex_digit_display_1 (.value(CPU_pc_out[31:28]));  // open: dp
  Clock clock_1 (.out(clock_1_out));
  Hex_Digit_Display hex_digit_display_2 (.value(CPU_pc_out[27:24]));  // open: dp
  Hex_Digit_Display hex_digit_display_3 (.value(CPU_pc_out_3));  // open: dp
  D_Flip_Flop d_ff_1 (.clk(clock_1_out), .D(1'b1), .Qn(d_ff_1_qn));  // open: Q, preset, en, reset
  Clock clock_2 (.out(clock_2_out));
  Button button_1 (.out(button_1_out));
  Hex_Digit_Display hex_digit_display_4 (.value(CPU_pc_out[15:12]));  // open: dp
  Hex_Digit_Display hex_digit_display_5 (.value(CPU_pc_out_2));  // open: dp
  CPU CPU (
    .Start_Addr_in(32'h400000), .Reset_in(d_ff_1_qn), .Data_in(Data_in), .Address(Address),
    .Data_out(Data_out), .MemRead(MemRead), .MemWrite(MemWrite),
    .unsupported_instruction(CPU_unsupported_instruction), .hold_in(s_r_ff_1_q),
    .PC_out({CPU_pc_out[31:24], CPU_pc_out_3, CPU_pc_out_2, CPU_pc_out[15:0]}));
  S_R_Flip_Flop s_r_ff_1 (
    .S(CPU_unsupported_instruction), .clk(clock_2_out), .R(1'b0), .Q(s_r_ff_1_q), .reset(button_1_out));  // open: Qn, preset, en
  LED led_1 (.in(s_r_ff_1_q));
  Hex_Digit_Display hex_digit_display_6 (.value(CPU_pc_out[7:4]));  // open: dp
  Hex_Digit_Display hex_digit_display_7 (.value(CPU_pc_out[11:8]));  // open: dp
  Hex_Digit_Display hex_digit_display_8 (.value(CPU_pc_out[3:0]));  // open: dp
  Comparator #(.width(24)) comparator_1 (.a(Address[31:8]), .b(24'hffff80), .eq(comparator_1_eq));  // open: gt, lt
  Comparator #(.width(16)) comparator_2 (.a(Address[31:16]), .b(16'h40), .eq(comparator_2_eq));  // open: gt, lt
  Comparator #(.width(16)) comparator_3 (.a(Address[31:16]), .b(16'h1000), .eq(comparator_3_eq));  // open: gt, lt
  Comparator #(.width(32)) comparator_4 (.a(Address), .b(32'hffff0010), .eq(comparator_4_eq));  // open: gt, lt
  and and_1 (and_1_out, comparator_1_eq, MemWrite);
  and and_2 (and_2_out, comparator_1_eq, MemRead);
  and and_3 (and_3_out, comparator_2_eq, MemRead);
  and and_4 (and_4_out, comparator_3_eq, MemWrite);
  and and_5 (and_5_out, comparator_3_eq, MemRead);
  and and_6 (and_6_out, comparator_4_eq, MemWrite);
  and and_7 (and_7_out, comparator_4_eq, MemRead);
  _7_Segment_Display u_7_segment_display_1 (
    .g(register_1_q[14]), .f(register_1_q[13]), .a(register_1_q[8]), .b(register_1_q[9]),
    .e(register_1_q[12]), .d(register_1_q[11]), .c(register_1_q[10]), .dp(register_1_q[15]));
  DotMatrix #(.inputtype("row"), .matrixcols(32), .matrixrows(32)) dotmatrix_1 (
    .row0(videoram_1__0), .row1(videoram_1__1), .row2(videoram_1__2), .row3(videoram_1__3),
    .row4(videoram_1__4), .row5(videoram_1__5), .row6(videoram_1__6), .row7(videoram_1__7),
    .row8(videoram_1__8), .row9(videoram_1__9), .row10(videoram_1__10), .row11(videoram_1__11),
    .row12(videoram_1__12), .row13(videoram_1__13), .row14(videoram_1__14), .row15(videoram_1__15),
    .row16(videoram_1__16), .row17(videoram_1__17), .row18(videoram_1__18), .row19(videoram_1__19),
    .row20(videoram_1__20), .row21(videoram_1__21), .row22(videoram_1__22), .row23(videoram_1__23),
    .row24(videoram_1__24), .row25(videoram_1__25), .row26(videoram_1__26), .row27(videoram_1__27),
    .row28(videoram_1__28), .row29(videoram_1__29), .row30(videoram_1__30), .row31(videoram_1__31));
  Videoram videoram_1 (
    .str(and_1_out), .Address(Address[6:2]), .Data_In(Data_out), .ld(and_2_out), ._0(videoram_1__0),
    ._8(videoram_1__8), ._16(videoram_1__16), ._24(videoram_1__24), ._1(videoram_1__1), ._9(videoram_1__9),
    ._17(videoram_1__17), ._25(videoram_1__25), ._2(videoram_1__2), ._10(videoram_1__10),
    ._18(videoram_1__18), ._26(videoram_1__26), ._3(videoram_1__3), ._11(videoram_1__11),
    ._19(videoram_1__19), ._27(videoram_1__27), ._4(videoram_1__4), ._12(videoram_1__12),
    ._20(videoram_1__20), ._28(videoram_1__28), ._5(videoram_1__5), ._13(videoram_1__13),
    ._21(videoram_1__21), ._29(videoram_1__29), ._6(videoram_1__6), ._14(videoram_1__14),
    ._22(videoram_1__22), ._30(videoram_1__30), ._7(videoram_1__7), ._15(videoram_1__15),
    ._23(videoram_1__23), ._31(videoram_1__31), .Data_Out(Data_in));
  Button button_2 (.out(rot));
  or or_1 (or_1_out, and_4_out, and_5_out);
  Register #(.width(32)) register_1 (.D(Data_out), .en(and_6_out), .Q(register_1_q), .clk(clock_3_out));  // open: clr
  Clock clock_3 (.out(clock_3_out));
  Button button_3 (.out(rt));
  Button button_4 (.out(lt));
  ROM #(.addrWidth(14), .dataWidth(32)) rom_1 (.addr(Address[15:2]), .data(Data_in), .sel(and_3_out));
  RAM #(.addrWidth(14), .dataWidth(32), .bus("separate")) ram_1 (
    .addr(Address[15:2]), .din(Data_out), .data(Data_in), .str(and_4_out), .sel(or_1_out), .clk(clock_4_out),
    .ld(and_5_out));  // open: clr
  Clock clock_4 (.out(clock_4_out));
  _7_Segment_Display u_7_segment_display_2 (
    .g(register_1_q[6]), .f(register_1_q[5]), .a(register_1_q[0]), .b(register_1_q[1]), .e(register_1_q[4]),
    .d(register_1_q[3]), .c(register_1_q[2]), .dp(register_1_q[7]));
  assign Data_in = and_7_out ? register_1_q : 32'bz;  // Controlled_Buffer controlled_buffer_1
  Clock clock_5 (.out(clock_5_out));
  Comparator #(.width(32)) comparator_5 (.a(Address), .b(32'hffff000c), .eq(comparator_5_eq));  // open: gt, lt
  TTY tty_1 (.data(Data_out[6:0]), .clk(clock_5_out), .we(and_8_out), .clr(button_5_out));
  Button button_5 (.out(button_5_out));
  and and_8 (and_8_out, comparator_5_eq, MemWrite);
  Clock clock_6 (.out(clock_6_out));
  Keyboard keyboard_1 (
    .clk(clock_6_out), .re(and_9_out), .clr(button_6_out), .avail(keyboard_1_avail), .data(keyboard_1_data));
  and and_9 (and_9_out, comparator_6_eq, MemRead);
  Comparator #(.width(32)) comparator_6 (.a(Address), .b(32'hffff0004), .eq(comparator_6_eq));  // open: gt, lt
  Comparator #(.width(32)) comparator_7 (.a(Address), .b(32'hffff0050), .eq(rst));  // open: gt, lt
  Button button_6 (.out(button_6_out));
  Multiplexer #(.enable("false")) multiplexer_1 (.in0(d_ff_2_q), .in1(1'b1), .out(multiplexer_1_out), .sel(rot));
  Multiplexer #(.enable("false")) multiplexer_2 (.in0(d_ff_3_q), .in1(1'b1), .out(multiplexer_2_out), .sel(lt));
  Multiplexer #(.enable("false")) multiplexer_3 (.in0(d_ff_4_q), .in1(1'b1), .out(multiplexer_3_out), .sel(rt));
  D_Flip_Flop d_ff_2 (.clk(clock_7_out), .D(multiplexer_1_out), .Q(d_ff_2_q), .reset(rst));  // open: Qn, preset, en
  Clock clock_7 (.out(clock_7_out));
  Clock clock_8 (.out(clock_8_out));
  and and_10 (and_10_out, multiplexer_2_out, d_ff_4_qn);
  Clock clock_9 (.out(clock_9_out));
  and and_11 (and_11_out, d_ff_3_qn, multiplexer_3_out);
  assign Data_in = and_9_out ? bit_extender_1_out : 32'bz;  // Controlled_Buffer controlled_buffer_2
  assign bit_extender_1_out = {{25{1'b0}}, keyboard_1_data};  // Bit_Extender bit_extender_1
  assign bit_extender_2_out = {{31{1'b0}}, keyboard_1_avail};  // Bit_Extender bit_extender_2
  assign Data_in = and_12_out ? bit_extender_2_out : 32'bz;  // Controlled_Buffer controlled_buffer_3
  and and_12 (and_12_out, comparator_8_eq, MemRead);
  Comparator #(.width(32)) comparator_8 (.a(Address), .b(32'hffff0000), .eq(comparator_8_eq));  // open: gt, lt
  D_Flip_Flop d_ff_3 (
    .clk(clock_8_out), .D(and_10_out), .Q(d_ff_3_q), .Qn(d_ff_3_qn), .reset(rst));  // open: preset, en
  D_Flip_Flop d_ff_4 (
    .clk(clock_9_out), .D(and_11_out), .Q(d_ff_4_q), .Qn(d_ff_4_qn), .reset(rst));  // open: preset, en
  assign Data_in = and_13_out ? 32'h1 : 32'bz;  // Controlled_Buffer controlled_buffer_4
  and and_13 (and_13_out, comparator_9_eq, MemRead);
  Comparator #(.width(32)) comparator_9 (.a(Address), .b(32'hffff0008), .eq(comparator_9_eq));  // open: gt, lt
  assign Data_in = and_14_out ? bit_extender_3_out : 32'bz;  // Controlled_Buffer controlled_buffer_5
  assign bit_extender_3_out = {{31{1'b0}}, d_ff_2_q};  // Bit_Extender bit_extender_3
  and and_14 (and_14_out, comparator_10_eq, MemRead);
  Comparator #(.width(32)) comparator_10 (.a(Address), .b(32'hffff004c), .eq(comparator_10_eq));  // open: gt, lt
  assign bit_extender_4_out = {{31{1'b0}}, d_ff_3_q};  // Bit_Extender bit_extender_4
  and and_15 (and_15_out, comparator_11_eq, MemRead);
  Comparator #(.width(32)) comparator_11 (.a(Address), .b(32'hffff0044), .eq(comparator_11_eq));  // open: gt, lt
  assign bit_extender_5_out = {{31{1'b0}}, d_ff_4_q};  // Bit_Extender bit_extender_5
  and and_16 (and_16_out, comparator_12_eq, MemRead);
  Comparator #(.width(32)) comparator_12 (.a(Address), .b(32'hffff0048), .eq(comparator_12_eq));  // open: gt, lt
  assign Data_in = and_15_out ? bit_extender_4_out : 32'bz;  // Controlled_Buffer controlled_buffer_6
  assign Data_in = and_16_out ? bit_extender_5_out : 32'bz;  // Controlled_Buffer controlled_buffer_7

  // Notes on the sheet:
  //   Start addr
  //   Reset circuit
  //   Data in -->
  //   press to continue
  //   PC
  //   Address -->
  //   Data out  -->
  //   CPU halted
  //   Rotate
  //   Left
  //   Right
  //   ROM
  //   contents of rom_1 (hex, n*v repeats v):
  //   fc10117 ffc10113 513 593 613 8000ef 6f fe010113 112e23 812c23 912a23 1212823 1312623 1412423 1512223
  //   1612023 3e4000ef 4014b7 a3848493 413 1900913 40593 4a503 47c000ef 140413 448493 ff2416e3 100009b7
  //   40000b37 fffb0b13 10000ab7 a8a93 401a37 a38a0a13 640006f 51000ef 6050663 564000ef 889a483 fff48413
  //   16484b3 249493 1548933 14484b3 92503 4a783 40593 f56533 418000ef 140413 490913 448493 889a783 378793
  //   fc87dce3 700000ef 50413 11000ef 2804663 7e4000ef f8050ee3 460000ef fa1ff06f 7ec000ef 50663 618000ef
  //   f91ff06f 590000ef f89ff06f 10000937 8892783 279793 401737 a3870493 10000437 7440693 f48633 100005b7
  //   58593 f585b3 400513 3a8000ef 7440793 8892703 271713 970733 1078613 7a683 d72023 478793 470713
  //   fec798e3 513 1c12083 1812403 1412483 1012903 c12983 812a03 412a83 12b03 2010113 8067 41f55793 a7c533
  //   40f50533 8067 ffff07b7 a7a623 8067 ffff07b7 a00713 e7a623 8067 54783 78c63 ffff0737 f72623 150513
  //   54783 fe079ae3 8067 ff010113 41f55813 2d87813 410713 900613 a00593 fff60613 2b567b3 41f7d693 f6c7b3
  //   40d787b3 3078793 f70423 2b54533 fff70713 fc051ee3 80663 ffff07b7 107a623 900793 2c7c263 410793
  //   c787b3 e10693 ffff0637 7c703 e62623 178793 fed79ae3 1010113 8067 ffff07b7 7a503 8067 ffff07b7 47a503
  //   8067 50693 100793 4b7d263 fff58613 513 ffff0737 a00593 72783 fe078ee3 472783 ff7f793 f68023 b78a63
  //   168693 150513 fec510e3 60513 68023 8067 fff00513 8067 100593 513 ffff0737 900613 100813 2d00893
  //   fff00313 200006f fd068793 2f66c63 251793 a787b3 179793 fd068693 f68533 72783 fe078ee3 472683
  //   fc051ce3 fd059ae3 fd1698e3 30593 fe5ff06f 2b50533 8067 ffff82b7 2000313 52383 72a023 428293 450513
  //   fff30313 fe0316e3 8067 297 5ac28293 1f37 234f0f13 1e2a023 a2a023 8067 297 59028293 2a303 10313
  //   131393 63c333 70037513 855513 fe0508e3 62a023 8067 100007b7 847a783 800613 40f60633 50713 100007b7
  //   887a783 279693 100007b7 78793 d787b3 1050513 72683 c696b3 d7a023 470713 478793 fea716e3 8067
  //   100007b7 887a683 269693 10000737 70713 d707b3 1070713 d706b3 7a703 40c75713 e7a023 478793 fed798e3
  //   8067 ff010113 112623 100007b7 f00713 8e7a623 100007b7 300713 8e7a423 100007b7 600713 8e7a223
  //   10000537 50513 4017b7 90878793 f07a703 6e52223 f47a703 6e52423 f87a703 6e52623 fc7a783 6f52823
  //   6450513 f1dff0ef c12083 1010113 8067 100007b7 8c7a783 10000737 70713 479693 4017b7 90878793 d787b3
  //   7a683 6d72223 47a683 6d72423 87a683 6d72623 c7a783 6f72823 8067 259593 ffff87b7 f585b3 a5a023 8067
  //   2a05863 58793 251513 a58533 7a703 62583 b76733 e6a023 478793 460613 468693 fea792e3 8067 2a05863
  //   58793 251513 a58533 7a703 62583 b77733 e6a023 478793 460613 468693 fea792e3 8067 ff010113 112623
  //   812423 100007b7 887a683 269693 10000737 70713 e687b3 1070413 8686b3 7a703 171713 e7a023 478793
  //   fed798e3 2cc000ef 2051263 10000737 8472783 fff78793 8f72223 c12083 812403 1010113 8067 100513
  //   c29ff0ef 100007b7 887a703 271713 100007b7 78793 f707b3 870433 7a703 40175713 e7a023 478793 fe8798e3
  //   fb9ff06f ff010113 112623 812423 100513 be1ff0ef 100007b7 887a683 269693 10000737 70713 e687b3
  //   1070413 8686b3 7a703 40175713 e7a023 478793 fed798e3 220000ef 2050c63 100007b7 887a683 269693
  //   100007b7 78793 f687b3 8686b3 7a703 171713 e7a023 478793 fed798e3 140006f 10000737 8472783 178793
  //   8f72223 c12083 812403 1010113 8067 100007b7 887a603 261693 10000737 70713 e687b3 fec70713 d70733
  //   c7a683 d7a823 ffc78793 fee79ae3 160613 100007b7 8c7a423 8067 100007b7 887a703 fff70613 271693
  //   10000737 70713 e687b3 1470713 d70733 7a683 fed7ae23 478793 fee79ae3 100007b7 8c7a423 8067 ff010113
  //   112623 100006b7 8c6a783 279713 4017b7 a9c78793 e787b3 7a783 8f6a623 11c000ef aa1ff0ef d49ff0ef
  //   110000ef a95ff0ef c95ff0ef 104000ef a89ff0ef 10000537 6450513 c35ff0ef f0000ef a75ff0ef e8000ef
  //   51863 c12083 1010113 8067 100006b7 4017b7 a9c78793 8c6a703 271713 e78733 72703 271713 e78733 72703
  //   271713 e787b3 7a783 8f6a623 cd1ff0ef c25ff0ef 10000537 6450513 bcdff0ef fa9ff06f ff010113 112623
  //   812423 912223 eb1ff0ef 100007b7 887a783 279793 100006b7 7468493 7468693 401637 a3860613 f60633
  //   100005b7 58593 f585b3 400513 cfdff0ef 4a403 44a783 f46433 84a783 f46433 c4a783 f46433 e99ff0ef 40513
  //   c12083 81240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
  //   RAM
  //   TDR
  //   RDR
  //   clear
  //   RISC-V RV32IM Computer System model by Pavel Gladyshev
  //   MMIO DIsplay
  //   MMIO Keyboard
  //   clear
  //   clear
  //   licensed under Creative Commons Attribution International license 4.0 
  //   RCR
  //   TCR
  //   Rotate
  //   Display is always ready
  //   clear
  //   Left
  //   Right
  //   clear
  //   clear
  //   clear
  //   clear
endmodule

// RISC-V RV32IM
module CPU (
  input  [31:0] Start_Addr_in,
  input  Reset_in,
  input  [31:0] Data_in,
  input  hold_in,
  output [31:0] Address,
  output [31:0] Data_out,
  output MemRead,
  output MemWrite,
  output [31:0] PC_out,
  output unsupported_instruction
);

  wire A___B_signed, A___B_unsigned, A__B, clock_1_out, clock_2_out, clock_3_out, div_by_zero, execute,
       fetch, not_1_out, not_2_out, or_1_out, or_2_out, sel_address_source, sel_byte_out, sel_halfword_out,
       sel_IR_store, sel_reg_write_enable;
  wire [1:0] sel_B_source, sel_PC_increment, sel_PC_source;
  wire [2:0] funct3, sel_muldiv_opcode;
  wire [3:0] sel_alu_opcode, sel_rd_source;
  wire [4:0] rd_addr, rs1_addr, rs2_addr;
  wire [6:0] funct7, opcode;
  wire [31:0] Addr, ALU_out, B_immediate, byte_sign_extended, byte_zero_extended, halfword_sign_extended,
       halfword_zero_extended, I_immediate_Sign, I_immediate_Unsign, IR_q, J_immediate, MulDiv_out,
       multiplexer_1_out, multiplexer_2_out, multiplexer_3_out, multiplexer_4_out, multiplexer_5_out, PC_4,
       PC_updated, Register_bank_r1, rs2_out, S_immediate, U_immediate, word_in;

  Input_data_selector input_data_selector_1 (
    .Address_2(Addr[1:0]), .Data_In(Data_in), .byte_sign_extended(byte_sign_extended),
    .byte_zero_extended(byte_zero_extended), .halfword_sign_extended(halfword_sign_extended),
    .halfword_zero_extended(halfword_zero_extended), .Word(word_in));
  Register #(.width(32)) IR (.D(word_in), .en(sel_IR_store), .Q(IR_q), .clk(clock_1_out));  // open: clr
  Clock clock_1 (.out(clock_1_out));
  Instruction_splitter instruction_splitter_1 (
    .Instruction_Code(IR_q), .opcode(opcode), .rd(rd_addr), .funct3(funct3), .rs1(rs1_addr),
    .I_immediate_Signed(I_immediate_Sign), .J_immediate(J_immediate), .rs2(rs2_addr), .funct7(funct7),
    .S_immediate(S_immediate), .U_immediate(U_immediate), .B_immediate(B_immediate),
    .I_immediate_Unsigned(I_immediate_Unsign));
  Multiplexer #(.width(32), .enable("false")) multiplexer_1 (
    .in0(multiplexer_2_out), .in1(Start_Addr_in), .out(multiplexer_1_out), .sel(Reset_in));
  Register #(.width(32)) PC (.D(multiplexer_1_out), .en(not_1_out), .Q(PC_out), .clk(clock_2_out));  // open: clr
  not not_1 (not_1_out, hold_in);
  Clock clock_2 (.out(clock_2_out));
  Multiplexer #(.select(2), .width(32), .enable("false")) multiplexer_2 (
    .in0(PC_out), .in1(PC_4), .in2(ALU_out), .in3(PC_updated), .out(multiplexer_2_out), .sel(sel_PC_source));
  Multiplexer #(.select(2), .width(32), .enable("false")) multiplexer_3 (
    .in0(J_immediate), .in1(B_immediate), .in2(U_immediate), .in3(U_immediate), .out(multiplexer_3_out),
    .sel(sel_PC_increment));
  Adder #(.width(32)) adder_1 (.a(multiplexer_3_out), .b(PC_out), .out(PC_updated));  // open: cin, cout
  Adder #(.width(32)) adder_2 (.a(32'h4), .b(PC_out), .out(PC_4));  // open: cin, cout
  Multiplexer #(.select(4), .width(32), .disabled(0), .enable("false")) multiplexer_4 (
    .in0(ALU_out), .in1(U_immediate), .in2(byte_sign_extended), .in3(byte_zero_extended),
    .in4(halfword_sign_extended), .in5(halfword_zero_extended), .in6(PC_updated), .in7(word_in), .in8(PC_4),
    .in9(MulDiv_out), .out(multiplexer_4_out), .sel(sel_rd_source));  // open: in10, in11, in12, in13, in14, in15
  Clock clock_3 (.out(clock_3_out));
  or or_1 (or_1_out, Reset_in, hold_in);
  D_Flip_Flop Control_state (
    .clk(clock_3_out), .D(fetch), .Q(execute), .Qn(fetch), .en(not_2_out));  // open: preset, reset
  not not_2 (not_2_out, or_1_out);
  Register_bank Register_bank (
    .RegWr(sel_reg_write_enable), .AW(rd_addr), .Data_In(multiplexer_4_out), .AR1(rs1_addr), .AR2(rs2_addr),
    .R1(Register_bank_r1), .R2(rs2_out));
  multiplied_divider Mul_Div (
    .A(Register_bank_r1), .B(rs2_out), .opcode(sel_muldiv_opcode), .muldiv_out(MulDiv_out),
    .div_by_zero(div_by_zero));
  Multiplexer #(.select(2), .width(32), .enable("false")) multiplexer_5 (
    .in0(rs2_out), .in1(I_immediate_Sign), .in2(I_immediate_Unsign), .in3(S_immediate),
    .out(multiplexer_5_out), .sel(sel_B_source));
  Instruction_decoder instruction_decoder_1 (
    .funct7(funct7), .opcode(opcode), .funct3(funct3), .execute(execute),
    .sel_PC_increment(sel_PC_increment), .sel_PC_source(sel_PC_source), .fetch(fetch),
    .sel_IR_store(sel_IR_store), .sel_address_source(sel_address_source), .MemRead(MemRead),
    .MemWrite(MemWrite), .operation_code(sel_alu_opcode), .sel_B_source(sel_B_source),
    .sel_rd_source(sel_rd_source), .sel_halfword_out(sel_halfword_out), .sel_byte_out(sel_byte_out),
    .sel_reg_write_enable(sel_reg_write_enable), .A__B(A__B), .A___B_signed(A___B_signed),
    .A___B_unsigned(A___B_unsigned), .sel_muldiv_opcode(sel_muldiv_opcode), .div_by_zero(div_by_zero),
    .halt(unsupported_instruction), .I_immediate(I_immediate_Unsign[11:0]));
  ALU ALU (
    .operation_code(sel_alu_opcode), .A(Register_bank_r1), .B(multiplexer_5_out), .Result(ALU_out),
    .out_4(A__B), .Signed(A___B_signed), .Unsigned(A___B_unsigned));
  Multiplexer #(.width(32), .disabled(0), .enable("false")) multiplexer_6 (
    .in0(ALU_out), .in1(PC_out), .out(Addr), .sel(sel_address_source));
  assign Address = or_2_out ? {Addr[31:2], 2'b00} : 32'bz;  // Controlled_Buffer controlled_buffer_1
  or or_2 (or_2_out, MemRead, MemWrite);
  Output_data_composer output_data_composer_1 (
    .Address_2(Addr[1:0]), .Sel({sel_byte_out, sel_halfword_out}), .New_data(rs2_out), .Old_data(Data_in),
    .OutputEnable(MemWrite), .Data_out(Data_out));

  // Other names for the same wires on the sheet: PC[31:0] = PC_out; unsupported_inst_out = unsupported_instruction

  // Notes on the sheet:
  //   Address circuits
  //   Data path
  //   Control
endmodule

module Register_bank (
  input  RegWr,
  input  [4:0] AW,
  input  [31:0] Data_In,
  input  [4:0] AR1,
  input  [4:0] AR2,
  output [31:0] R1,
  output [31:0] R2
);

  wire clock_1_out, clock_2_out, clock_3_out, clock_4_out, clock_5_out, clock_6_out, clock_7_out,
       clock_8_out, clock_9_out, clock_10_out, clock_11_out, clock_12_out, clock_13_out, clock_14_out,
       clock_15_out, clock_16_out, clock_17_out, clock_18_out, clock_19_out, clock_20_out, clock_21_out,
       clock_22_out, clock_23_out, clock_24_out, clock_25_out, clock_26_out, clock_27_out, clock_28_out,
       clock_29_out, clock_30_out, clock_31_out;
  wire [3:0] decoder_1_out0, decoder_1_out4, decoder_1_out8, decoder_1_out12, decoder_1_out16,
       decoder_1_out20, decoder_1_out24, decoder_1_out28;
  wire [31:0] o1, o2, o3, o4, o5, o6, o7, o8, o9, o10, o11, o12, o13, o14, o15, o16, o17, o18, o19, o20, o21,
       o22, o23, o24, o25, o26, o27, o28, o29, o30, o31;

  Clock clock_1 (.out(clock_1_out));
  Clock clock_2 (.out(clock_2_out));
  Clock clock_3 (.out(clock_3_out));
  Register #(.width(32)) x1__ra (.D(Data_In), .en(decoder_1_out0[1]), .Q(o1), .clk(clock_1_out), .clr(1'b0));
  Register #(.width(32)) x2__sp (.D(Data_In), .en(decoder_1_out0[2]), .Q(o2), .clk(clock_2_out), .clr(1'b0));
  Register #(.width(32)) x3__gp (.D(Data_In), .en(decoder_1_out0[3]), .Q(o3), .clk(clock_3_out), .clr(1'b0));
  Clock clock_4 (.out(clock_4_out));
  Clock clock_5 (.out(clock_5_out));
  Clock clock_6 (.out(clock_6_out));
  Clock clock_7 (.out(clock_7_out));
  Multiplexer #(.select(5), .width(32), .enable("false")) multiplexer_1 (
    .in0({32{1'b0}}), .in1(o1), .in2(o2), .in3(o3), .in4(o4), .in5(o5), .in6(o6), .in7(o7), .in8(o8),
    .in9(o9), .in10(o10), .in11(o11), .in12(o12), .in13(o13), .in14(o14), .in15(o15), .in16(o16), .in17(o17),
    .in18(o18), .in19(o19), .in20(o20), .in21(o21), .in22(o22), .in23(o23), .in24(o24), .in25(o25),
    .in26(o26), .in27(o27), .in28(o28), .in29(o29), .in30(o30), .in31(o31), .out(R1), .sel(AR1));
  Register #(.width(32)) x4__tp (.D(Data_In), .en(decoder_1_out4[0]), .Q(o4), .clk(clock_4_out), .clr(1'b0));
  Register #(.width(32)) x5__t0 (.D(Data_In), .en(decoder_1_out4[1]), .Q(o5), .clk(clock_5_out), .clr(1'b0));
  Register #(.width(32)) x6__t1 (.D(Data_In), .en(decoder_1_out4[2]), .Q(o6), .clk(clock_6_out), .clr(1'b0));
  Register #(.width(32)) x7__t2 (.D(Data_In), .en(decoder_1_out4[3]), .Q(o7), .clk(clock_7_out), .clr(1'b0));
  Decoder #(.select(5), .disabled(0)) decoder_1 (
    .out0(decoder_1_out0[0]), .out1(decoder_1_out0[1]), .out2(decoder_1_out0[2]), .out3(decoder_1_out0[3]),
    .out4(decoder_1_out4[0]), .out5(decoder_1_out4[1]), .out6(decoder_1_out4[2]), .out7(decoder_1_out4[3]),
    .out8(decoder_1_out8[0]), .out9(decoder_1_out8[1]), .out10(decoder_1_out8[2]), .out11(decoder_1_out8[3]),
    .out12(decoder_1_out12[0]), .out13(decoder_1_out12[1]), .out14(decoder_1_out12[2]),
    .out15(decoder_1_out12[3]), .out16(decoder_1_out16[0]), .out17(decoder_1_out16[1]),
    .out18(decoder_1_out16[2]), .out19(decoder_1_out16[3]), .out20(decoder_1_out20[0]),
    .out21(decoder_1_out20[1]), .out22(decoder_1_out20[2]), .out23(decoder_1_out20[3]),
    .out24(decoder_1_out24[0]), .out25(decoder_1_out24[1]), .out26(decoder_1_out24[2]),
    .out27(decoder_1_out24[3]), .out28(decoder_1_out28[0]), .out29(decoder_1_out28[1]),
    .out30(decoder_1_out28[2]), .out31(decoder_1_out28[3]), .sel(AW), .en(RegWr));
  Clock clock_8 (.out(clock_8_out));
  Clock clock_9 (.out(clock_9_out));
  Clock clock_10 (.out(clock_10_out));
  Clock clock_11 (.out(clock_11_out));
  Register #(.width(32)) x8__s0___fp (.D(Data_In), .en(decoder_1_out8[0]), .Q(o8), .clk(clock_8_out), .clr(1'b0));
  Register #(.width(32)) x9__s1 (.D(Data_In), .en(decoder_1_out8[1]), .Q(o9), .clk(clock_9_out), .clr(1'b0));
  Register #(.width(32)) x10__a0 (.D(Data_In), .en(decoder_1_out8[2]), .Q(o10), .clk(clock_10_out), .clr(1'b0));
  Register #(.width(32)) x11__a1 (.D(Data_In), .en(decoder_1_out8[3]), .Q(o11), .clk(clock_11_out), .clr(1'b0));
  Clock clock_12 (.out(clock_12_out));
  Clock clock_13 (.out(clock_13_out));
  Clock clock_14 (.out(clock_14_out));
  Clock clock_15 (.out(clock_15_out));
  Register #(.width(32)) x12__a2 (.D(Data_In), .en(decoder_1_out12[0]), .Q(o12), .clk(clock_12_out), .clr(1'b0));
  Register #(.width(32)) x13__a3 (.D(Data_In), .en(decoder_1_out12[1]), .Q(o13), .clk(clock_13_out), .clr(1'b0));
  Register #(.width(32)) x14__a4 (.D(Data_In), .en(decoder_1_out12[2]), .Q(o14), .clk(clock_14_out), .clr(1'b0));
  Register #(.width(32)) x15__a5 (.D(Data_In), .en(decoder_1_out12[3]), .Q(o15), .clk(clock_15_out), .clr(1'b0));
  Clock clock_16 (.out(clock_16_out));
  Clock clock_17 (.out(clock_17_out));
  Clock clock_18 (.out(clock_18_out));
  Clock clock_19 (.out(clock_19_out));
  Register #(.width(32)) x16__a6 (.D(Data_In), .en(decoder_1_out16[0]), .Q(o16), .clk(clock_16_out), .clr(1'b0));
  Register #(.width(32)) x17__a7 (.D(Data_In), .en(decoder_1_out16[1]), .Q(o17), .clk(clock_17_out), .clr(1'b0));
  Register #(.width(32)) x18__s2 (.D(Data_In), .en(decoder_1_out16[2]), .Q(o18), .clk(clock_18_out), .clr(1'b0));
  Register #(.width(32)) x19__s3 (.D(Data_In), .en(decoder_1_out16[3]), .Q(o19), .clk(clock_19_out), .clr(1'b0));
  Register #(.width(32)) x20__s4 (.D(Data_In), .en(decoder_1_out20[0]), .Q(o20), .clk(clock_20_out), .clr(1'b0));
  Clock clock_20 (.out(clock_20_out));
  Register #(.width(32)) x21__s5 (.D(Data_In), .en(decoder_1_out20[1]), .Q(o21), .clk(clock_21_out), .clr(1'b0));
  Clock clock_21 (.out(clock_21_out));
  Register #(.width(32)) x22__s6 (.D(Data_In), .en(decoder_1_out20[2]), .Q(o22), .clk(clock_22_out), .clr(1'b0));
  Clock clock_22 (.out(clock_22_out));
  Register #(.width(32)) x23__s7 (.D(Data_In), .en(decoder_1_out20[3]), .Q(o23), .clk(clock_23_out), .clr(1'b0));
  Clock clock_23 (.out(clock_23_out));
  Register #(.width(32)) x24__s8 (.D(Data_In), .en(decoder_1_out24[0]), .Q(o24), .clk(clock_24_out), .clr(1'b0));
  Clock clock_24 (.out(clock_24_out));
  Register #(.width(32)) x25__s9 (.D(Data_In), .en(decoder_1_out24[1]), .Q(o25), .clk(clock_25_out), .clr(1'b0));
  Clock clock_25 (.out(clock_25_out));
  Register #(.width(32)) x26__s10 (.D(Data_In), .en(decoder_1_out24[2]), .Q(o26), .clk(clock_26_out), .clr(1'b0));
  Clock clock_26 (.out(clock_26_out));
  Register #(.width(32)) x27__s11 (.D(Data_In), .en(decoder_1_out24[3]), .Q(o27), .clk(clock_27_out), .clr(1'b0));
  Clock clock_27 (.out(clock_27_out));
  Multiplexer #(.select(5), .width(32), .enable("false")) multiplexer_2 (
    .in0({32{1'b0}}), .in1(o1), .in2(o2), .in3(o3), .in4(o4), .in5(o5), .in6(o6), .in7(o7), .in8(o8),
    .in9(o9), .in10(o10), .in11(o11), .in12(o12), .in13(o13), .in14(o14), .in15(o15), .in16(o16), .in17(o17),
    .in18(o18), .in19(o19), .in20(o20), .in21(o21), .in22(o22), .in23(o23), .in24(o24), .in25(o25),
    .in26(o26), .in27(o27), .in28(o28), .in29(o29), .in30(o30), .in31(o31), .out(R2), .sel(AR2));
  Register #(.width(32)) x28__t3 (.D(Data_In), .en(decoder_1_out28[0]), .Q(o28), .clk(clock_28_out), .clr(1'b0));
  Clock clock_28 (.out(clock_28_out));
  Register #(.width(32)) x29__t4 (.D(Data_In), .en(decoder_1_out28[1]), .Q(o29), .clk(clock_29_out), .clr(1'b0));
  Clock clock_29 (.out(clock_29_out));
  Register #(.width(32)) x30__t5 (.D(Data_In), .en(decoder_1_out28[2]), .Q(o30), .clk(clock_30_out), .clr(1'b0));
  Clock clock_30 (.out(clock_30_out));
  Register #(.width(32)) x31__t6 (.D(Data_In), .en(decoder_1_out28[3]), .Q(o31), .clk(clock_31_out), .clr(1'b0));
  Clock clock_31 (.out(clock_31_out));

  // Other names for the same wires on the sheet: DI[31:0] = Data_In

  // Notes on the sheet:
  //   x0 (zero)
endmodule

module ALU (
  input  [3:0] operation_code,
  input  [31:0] A,
  input  [31:0] B,
  output out_4,
  output Signed,
  output Unsigned,
  output [31:0] Result
);

  wire [31:0] adder_1_out, and_1_out, or_1_out, shifter_1_out, shifter_2_out, shifter_3_out,
       subtractor_1_out, xor_1_out;

  assign and_1_out = A & B;  // AND_Gate and_1, 32 bits wide
  assign or_1_out = A | B;  // OR_Gate or_1, 32 bits wide
  Adder #(.width(32)) adder_1 (.a(A), .b(B), .out(adder_1_out), .cin(1'b0));  // open: cout
  Comparator #(.width(32)) comparator_1 (.a(A), .b(B), .eq(out_4), .lt(Signed));  // open: gt
  Comparator #(.width(32), .mode("unsigned")) comparator_2 (.a(A), .b(B), .lt(Unsigned));  // open: gt, eq
  Subtractor #(.width(32)) subtractor_1 (.a(A), .b(B), .out(subtractor_1_out), .bin(1'b0));  // open: bout
  assign xor_1_out = A ^ B;  // XOR_Gate xor_1, 32 bits wide
  Shifter #(.width(32)) shifter_1 (.in(A), .\dist (B[4:0]), .out(shifter_1_out));
  Shifter #(.width(32), .shift("lr")) shifter_2 (.in(A), .\dist (B[4:0]), .out(shifter_2_out));
  Shifter #(.width(32), .shift("ar")) shifter_3 (.in(A), .\dist (B[4:0]), .out(shifter_3_out));
  Multiplexer #(.select(4), .width(32), .enable("false")) multiplexer_1 (
    .in0(adder_1_out), .in1(shifter_1_out), .in2({{31{1'b0}}, Signed}), .in3({{31{1'b0}}, Unsigned}),
    .in4(xor_1_out), .in5(shifter_2_out), .in6(or_1_out), .in7(and_1_out), .in8(subtractor_1_out),
    .in13(shifter_3_out), .out(Result), .sel(operation_code));  // open: in9, in10, in11, in12, in14, in15

  // Notes on the sheet:
  //   Unsigned
  //   operation code = funct7[5]|funct3[2:0]
endmodule

module multiplied_divider (
  input  [31:0] A,
  input  [31:0] B,
  input  [2:0] opcode,
  output [31:0] muldiv_out,
  output div_by_zero
);

  wire and_1_out, and_2_out, nor_1_out, xor_1_out;
  wire [31:0] adder_1_out, divider_1_out, divider_1_rem, divider_2_out, divider_2_rem, multiplexer_1_out,
       multiplexer_2_out, multiplexer_3_out, multiplexer_4_out, multiplexer_5_out, multiplexer_6_out,
       multiplier_1_cout, multiplier_1_out, multiplier_2_out, multiplier_3_out, negator_1_out, negator_2_out,
       negator_3_out, negator_4_out;

  and and_1 (and_1_out, opcode[0], ~opcode[1], opcode[2]);  // AND_Gate
  Multiplexer #(.width(32), .disabled(0), .enable("false")) multiplexer_1 (
    .in0({32{1'b0}}), .in1({32{1'b1}}), .out(multiplexer_1_out), .sel(A[31]));
  Multiplexer #(.width(32), .disabled(0), .enable("false")) multiplexer_2 (
    .in0({32{1'b0}}), .in1({32{1'b1}}), .out(multiplexer_2_out), .sel(and_2_out));
  and and_2 (and_2_out, ~and_1_out, B[31]);  // AND_Gate
  Negator #(.width(32)) negator_1 (.in(A), .out(negator_1_out));
  Negator #(.width(32)) negator_2 (.in(B), .out(negator_2_out));
  Multiplexer #(.width(32), .disabled(0), .enable("false")) multiplexer_3 (
    .in0(A), .in1(negator_1_out), .out(multiplexer_3_out), .sel(A[31]));
  Multiplexer #(.width(32), .disabled(0), .enable("false")) multiplexer_4 (
    .in0(B), .in1(negator_2_out), .out(multiplexer_4_out), .sel(B[31]));
  Multiplier #(.width(32)) multiplier_1 (.a(A), .b(B), .out(multiplier_1_out), .cout(multiplier_1_cout));  // open: cin
  Multiplier #(.width(32)) multiplier_2 (
    .a(multiplexer_1_out), .b(B), .out(multiplier_2_out), .cin(multiplier_1_cout));  // open: cout
  Multiplier #(.width(32)) multiplier_3 (.a(A), .b(multiplexer_2_out), .out(multiplier_3_out));  // open: cin, cout
  xor xor_1 (xor_1_out, B[31], A[31]);
  Divider #(.width(32)) divider_1 (
    .a(multiplexer_3_out), .b(multiplexer_4_out), .out(divider_1_out), .rem(divider_1_rem));  // open: upper
  Divider #(.width(32)) divider_2 (.a(A), .b(B), .out(divider_2_out), .rem(divider_2_rem));  // open: upper
  Adder #(.width(32)) adder_1 (.a(multiplier_2_out), .b(multiplier_3_out), .out(adder_1_out));  // open: cin, cout
  Negator #(.width(32)) negator_3 (.in(divider_1_out), .out(negator_3_out));
  Negator #(.width(32)) negator_4 (.in(divider_1_rem), .out(negator_4_out));
  Multiplexer #(.width(32), .disabled(0), .enable("false")) multiplexer_5 (
    .in0(divider_1_out), .in1(negator_3_out), .out(multiplexer_5_out), .sel(xor_1_out));
  Multiplexer #(.width(32), .disabled(0), .enable("false")) multiplexer_6 (
    .in0(divider_1_rem), .in1(negator_4_out), .out(multiplexer_6_out), .sel(A[31]));
  Multiplexer #(.select(3), .width(32), .enable("false")) multiplexer_7 (
    .in0(multiplier_1_out), .in1(adder_1_out), .in2(adder_1_out), .in3(multiplier_1_cout),
    .in4(multiplexer_5_out), .in5(divider_2_out), .in6(multiplexer_6_out), .in7(divider_2_rem),
    .out(muldiv_out), .sel(opcode));
  nor nor_1 (nor_1_out, B[0], B[1], B[2], B[3], B[4], B[5], B[6], B[7], B[8], B[9], B[10], B[11], B[12], B[13], B[14], B[15], B[16], B[17], B[18], B[19], B[20], B[21], B[22], B[23], B[24], B[25], B[26], B[27], B[28], B[29], B[30], B[31]);
  and and_3 (div_by_zero, nor_1_out, opcode[2]);

  // Other names for the same wires on the sheet: dividend_sign = A[31]; division = opcode[2]

  // Notes on the sheet:
  //   same as funct3 code in muldiv
  //   A
  //   B
  //   mulhsu
  //   A<0
  //   B<0
  //   Multiplier
  //   Divider
  //   abs(A)
  //   abs(B)
  //   mul
  //   mulhu
  //   mulh/mulhsu
  //   div
  //   rem
  //   divu
  //   remu
endmodule

// Instruction split
module Instruction_splitter (
  input  [31:0] Instruction_Code,
  output [6:0] opcode,
  output [4:0] rd,
  output [2:0] funct3,
  output [4:0] rs1,
  output [31:0] I_immediate_Signed,
  output [31:0] J_immediate,
  output [4:0] rs2,
  output [6:0] funct7,
  output [31:0] S_immediate,
  output [31:0] U_immediate,
  output [31:0] B_immediate,
  output [31:0] I_immediate_Unsigned
);


  assign B_immediate = {{20{Instruction_Code[31]}}, Instruction_Code[7], Instruction_Code[30:25], Instruction_Code[11:8], 1'b0};
  assign funct3 = Instruction_Code[14:12];
  assign funct7 = Instruction_Code[31:25];
  assign I_immediate_Signed = {{21{Instruction_Code[31]}}, Instruction_Code[30:20]};
  assign I_immediate_Unsigned = {{20{1'b0}}, Instruction_Code[31:20]};
  assign J_immediate = {{12{Instruction_Code[31]}}, Instruction_Code[19:12], Instruction_Code[20], Instruction_Code[30:21], 1'b0};
  assign opcode = Instruction_Code[6:0];
  assign rd = Instruction_Code[11:7];
  assign rs1 = Instruction_Code[19:15];
  assign rs2 = Instruction_Code[24:20];
  assign S_immediate = {{21{Instruction_Code[31]}}, Instruction_Code[30:25], Instruction_Code[11:7]};
  assign U_immediate = {Instruction_Code[31:12], {12{1'b0}}};

  // Notes on the sheet:
  //   R-type
endmodule

module Instruction_decoder (
  input  [6:0] funct7,
  input  [2:0] funct3,
  input  [6:0] opcode,
  input  execute,
  input  fetch,
  input  A__B,
  input  A___B_signed,
  input  A___B_unsigned,
  input  div_by_zero,
  input  [11:0] I_immediate,
  output [1:0] sel_PC_increment,
  output [1:0] sel_PC_source,
  output sel_IR_store,
  output sel_address_source,
  output MemRead,
  output MemWrite,
  output [3:0] operation_code,
  output [1:0] sel_B_source,
  output [3:0] sel_rd_source,
  output sel_halfword_out,
  output sel_byte_out,
  output sel_reg_write_enable,
  output [2:0] sel_muldiv_opcode,
  output halt
);

  wire add, addi, \and , and_11_out, and_15_out, and_16_out, and_17_out, and_18_out, and_19_out, and_20_out,
       and_21_out, and_22_out, and_30_out, and_31_out, andi, arith, arith_imm, beq, bge, bgeu, blt, bltu,
       bne, branch, decoder_7_out1, decoder_7_out5, div, divu, ebreak, ecall, funct3_0x0, funct7_0x0,
       funct7_0x1, funct7_0x20, I_imm_0x0, I_imm_0x1, jal, jalr, lb, lbu, lh, lhu, load, lui, lw, mul,
       muldiv, mulh, mulsu, mulu, \or , or_2_out, or_3_out, or_4_out, or_5_out, or_6_out, or_7_out, ori, rem,
       remu, sll, slli, slt, slti, sltiu, sltu, sra, srai, srl, srli, sub, sw, system,
       unsupported_instruction, \xor , xori;
  wire [3:3] multiplexer_2_out;
  wire [6:0] multiplexer_1_out;

  Multiplexer #(.width(7), .enable("false")) multiplexer_1 (
    .in0({7{1'b0}}), .in1(opcode), .out(multiplexer_1_out), .sel(execute));
  and and_1 (funct7_0x1, funct7[0], ~funct7[1], ~funct7[2], ~funct7[3], ~funct7[4], ~funct7[5], ~funct7[6]);  // AND_Gate
  and and_2 (funct7_0x0, ~funct7[0], ~funct7[1], ~funct7[2], ~funct7[3], ~funct7[4], ~funct7[5], ~funct7[6]);  // AND_Gate
  and and_3 (funct7_0x20, ~funct7[0], ~funct7[1], ~funct7[2], ~funct7[3], ~funct7[4], funct7[5], ~funct7[6]);  // AND_Gate
  nor nor_1 (funct3_0x0, funct3[0], funct3[1], funct3[2]);
  and and_4 (arith, multiplexer_1_out[0], multiplexer_1_out[1], ~multiplexer_1_out[2], ~multiplexer_1_out[3], multiplexer_1_out[4], multiplexer_1_out[5], ~multiplexer_1_out[6]);  // AND_Gate
  and and_5 (arith_imm, multiplexer_1_out[0], multiplexer_1_out[1], ~multiplexer_1_out[2], ~multiplexer_1_out[3], multiplexer_1_out[4], ~multiplexer_1_out[5], ~multiplexer_1_out[6]);  // AND_Gate
  and and_6 (load, multiplexer_1_out[0], multiplexer_1_out[1], ~multiplexer_1_out[2], ~multiplexer_1_out[3], ~multiplexer_1_out[4], ~multiplexer_1_out[5], ~multiplexer_1_out[6]);  // AND_Gate
  and and_7 (MemWrite, multiplexer_1_out[0], multiplexer_1_out[1], ~multiplexer_1_out[2], ~multiplexer_1_out[3], ~multiplexer_1_out[4], multiplexer_1_out[5], ~multiplexer_1_out[6]);  // AND_Gate
  and and_8 (branch, multiplexer_1_out[0], multiplexer_1_out[1], ~multiplexer_1_out[2], ~multiplexer_1_out[3], ~multiplexer_1_out[4], multiplexer_1_out[5], multiplexer_1_out[6]);  // AND_Gate
  and and_9 (lui, multiplexer_1_out[0], multiplexer_1_out[1], multiplexer_1_out[2], ~multiplexer_1_out[3], multiplexer_1_out[4], multiplexer_1_out[5], ~multiplexer_1_out[6]);  // AND_Gate
  and and_10 (jal, multiplexer_1_out[0], multiplexer_1_out[1], multiplexer_1_out[2], multiplexer_1_out[3], ~multiplexer_1_out[4], multiplexer_1_out[5], multiplexer_1_out[6]);  // AND_Gate
  and and_11 (and_11_out, multiplexer_1_out[0], multiplexer_1_out[1], multiplexer_1_out[2], ~multiplexer_1_out[3], ~multiplexer_1_out[4], multiplexer_1_out[5], multiplexer_1_out[6]);  // AND_Gate
  and and_12 (system, multiplexer_1_out[0], multiplexer_1_out[1], ~multiplexer_1_out[2], ~multiplexer_1_out[3], multiplexer_1_out[4], multiplexer_1_out[5], multiplexer_1_out[6]);  // AND_Gate
  and and_13 (sel_PC_increment[1], multiplexer_1_out[0], multiplexer_1_out[1], multiplexer_1_out[2], ~multiplexer_1_out[3], multiplexer_1_out[4], ~multiplexer_1_out[5], ~multiplexer_1_out[6]);  // AND_Gate
  and and_14 (jalr, funct3_0x0, and_11_out);
  Decoder #(.select(3), .disabled(0)) decoder_1 (
    .out0(lb), .out1(lh), .out2(lw), .out4(lbu), .out5(lhu), .sel(funct3), .en(load));  // open: out3, out6, out7
  Decoder #(.select(3), .disabled(0)) decoder_2 (
    .out0(beq), .out1(bne), .out4(blt), .out5(bge), .out6(bltu), .out7(bgeu), .sel(funct3), .en(branch));  // open: out2, out3
  Decoder #(.select(3), .disabled(0)) decoder_3 (
    .out0(add), .out1(sll), .out2(slt), .out3(sltu), .out4(\xor ), .out5(srl), .out6(\or ), .out7(\and ),
    .sel(funct3), .en(and_15_out));
  and and_15 (and_15_out, arith, funct7_0x0);
  Decoder #(.select(3), .disabled(0)) decoder_4 (
    .out0(sub), .out5(sra), .sel(funct3), .en(and_16_out));  // open: out1, out2, out3, out4, out6, out7
  and and_16 (and_16_out, arith, funct7_0x20);
  and and_17 (and_17_out, beq, A__B);
  and and_18 (and_18_out, ~A__B, bne);  // AND_Gate
  and and_19 (and_19_out, blt, A___B_signed);
  and and_20 (and_20_out, ~A___B_signed, bge);  // AND_Gate
  and and_21 (and_21_out, bltu, A___B_unsigned);
  and and_22 (and_22_out, ~A___B_unsigned, bgeu);  // AND_Gate
  Decoder #(.select(3), .disabled(0)) decoder_5 (
    .out0(sel_byte_out), .out1(sel_halfword_out), .out2(sw), .sel(funct3), .en(MemWrite));  // open: out3, out4, out5, out6, out7
  or or_1 (sel_PC_increment[0], and_17_out, and_18_out, and_19_out, and_20_out, and_21_out, and_22_out);
  Decoder #(.select(3), .disabled(0)) decoder_6 (
    .out0(mul), .out1(mulh), .out2(mulsu), .out3(mulu), .out4(div), .out5(divu), .out6(rem), .out7(remu),
    .sel(funct3), .en(muldiv));
  and and_23 (muldiv, arith, funct7_0x1);
  Decoder #(.select(3), .disabled(0)) decoder_7 (
    .out0(addi), .out1(decoder_7_out1), .out2(slti), .out3(sltiu), .out4(xori), .out5(decoder_7_out5),
    .out6(ori), .out7(andi), .sel(funct3), .en(arith_imm));
  and and_24 (slli, decoder_7_out1, funct7_0x0);
  and and_25 (srai, decoder_7_out5, funct7_0x20);
  and and_26 (srli, decoder_7_out5, funct7_0x0);
  Comparator #(.width(12), .mode("unsigned")) comparator_1 (
    .a(I_immediate), .b({12{1'b0}}), .eq(I_imm_0x0));  // open: gt, lt
  Comparator #(.width(12), .mode("unsigned")) comparator_2 (
    .a(I_immediate), .b(12'h1), .eq(I_imm_0x1));  // open: gt, lt
  and and_27 (ebreak, I_imm_0x1, system, funct3_0x0);
  and and_28 (ecall, system, funct3_0x0, I_imm_0x0);
  or or_2 (or_2_out, beq, bne, blt, bge, bltu, bgeu, sel_byte_out, sel_halfword_out, sw, lh, lb, lhu, lw, slli, lbu, srai, srli, sltiu, addi, andi, slti, ori, add, xori, slt, sll, \xor , sltu, \or , srl, \and , sub);
  or or_3 (or_3_out, or_2_out, sra, ebreak, ecall, muldiv, jalr, lui, jal, sel_PC_increment[1]);
  and and_29 (unsupported_instruction, ~or_3_out, execute);  // AND_Gate
  and and_30 (and_30_out, srai, arith_imm);
  Multiplexer #(.enable("false")) multiplexer_2 (
    .in0(and_30_out), .in1(funct7_0x20), .out(multiplexer_2_out[3]), .sel(arith));
  and and_31 (and_31_out, muldiv, funct3[2], div_by_zero);
  or or_4 (or_4_out, sel_PC_increment[0], jal);
  or or_5 (or_5_out, load, arith_imm, jalr);
  or or_6 (or_6_out, jal, jalr);
  Multiplexer #(.width(4), .enable("false")) multiplexer_3 (
    .in0(4'b0000), .in1({multiplexer_2_out[3], funct3}), .out(operation_code), .sel(or_7_out));
  or or_7 (or_7_out, arith, arith_imm);
  Priority_Encoder #(.select(2)) priority_encoder_1 (
    .in0(1'b1), .in1(execute), .in2(jalr), .in3(or_4_out), .out(sel_PC_source));  // open: gs, en_out, en_in
  or or_8 (MemRead, fetch, load, MemWrite);
  Priority_Encoder #(.select(2)) priority_encoder_2 (
    .in0(1'b1), .in1(or_5_out), .in2(sltiu), .in3(MemWrite), .out(sel_B_source));  // open: gs, en_out, en_in
  Priority_Encoder #(.select(4)) priority_encoder_3 (
    .in0(1'b1), .in1(lui), .in2(lb), .in3(lbu), .in4(lh), .in5(lhu), .in6(sel_PC_increment[1]), .in7(lw),
    .in8(or_6_out), .in9(muldiv), .out(sel_rd_source));  // open: in10, in11, in12, in13, in14, in15, gs, en_out, en_in
  or or_9 (sel_reg_write_enable, sel_PC_increment[1], arith_imm, arith, load, jalr, lui, jal, muldiv);
  or or_10 (halt, unsupported_instruction, and_31_out, ebreak);

  assign sel_address_source = fetch;
  assign sel_IR_store = fetch;
  assign sel_muldiv_opcode = funct3;

  // Other names for the same wires on the sheet: I_imm[11:0] = I_immediate; sb = sel_byte_out;
  //   do_branch = sel_PC_increment[0]; auipc = sel_PC_increment[1]; sh = sel_halfword_out; store = MemWrite

  // Notes on the sheet:
  //   Arithmetic instrucitons
  //   Load instructions
  //   Branch instructions
  //   Store instructions
  //   multiplication and division
  //   Arithmetic instrucitons with immediate operand
  //   system instructions (t.b.d.)
  //   illegal instruction detection
  //   0=ALU out, 1=PC
  //   01 = PC+4
  //   10 = ALU-out
  //   00 = rs2
  //   0000 = ALU out
  //   0001 = U-immediate
  //   1000 = PC+4
  //   1001 = MulDiv output
  //   00 = PC+J-immediate (jal)
  //   01 = PC+B-immediate
  //   1x = PC+U-immediate
  //   00 = PC  (PC is unchanged)
  //   11 = Incremented PC (see sel-PC-increment)
  //   01 = I-immediate-sign-extended
  //   10 = I-immediate-zero-extended
  //   11 = S-immediate-sign-extended
  //   0010 = byte from memory sign extended
  //   0011 = byte from memory zero extended
  //   0100 = halfword from memory sign extended
  //   0101 = halfword from memory zero extended
  //   0110 = Incremented PC (see sel-PC-increment)
  //   0111 = word from memory
endmodule

module Input_data_selector (
  input  [1:0] Address_2,
  input  [31:0] Data_In,
  output [31:0] byte_sign_extended,
  output [31:0] byte_zero_extended,
  output [31:0] halfword_sign_extended,
  output [31:0] halfword_zero_extended,
  output [31:0] Word
);

  Multiplexer #(.select(2), .width(8), .enable("false")) multiplexer_1 (
    .in0(Data_In[7:0]), .in1(Data_In[15:8]), .in2(Data_In[23:16]), .in3(Data_In[31:24]),
    .out({byte_sign_extended[31], byte_sign_extended[6:0]}), .sel(Address_2));
  Multiplexer #(.width(16), .enable("false")) multiplexer_2 (
    .in0(Data_In[15:0]), .in1(Data_In[31:16]),
    .out({halfword_sign_extended[31], halfword_sign_extended[14:0]}), .sel(Address_2[1]));

  assign byte_sign_extended[30:7] = {24{byte_sign_extended[31]}};
  assign byte_zero_extended = {{24{1'b0}}, byte_sign_extended[31], byte_sign_extended[6:0]};
  assign halfword_sign_extended[30:15] = {16{halfword_sign_extended[31]}};
  assign halfword_zero_extended = {{16{1'b0}}, halfword_sign_extended[31], halfword_sign_extended[14:0]};
  assign Word = Data_In;

  // Notes on the sheet:
  //   Data selector circuit. Picks half words and byte output based on the least significant bits of address
endmodule

module Output_data_composer (
  input  [1:0] Address_2,
  input  [1:0] Sel,
  input  [31:0] New_data,
  input  [31:0] Old_data,
  input  OutputEnable,
  output [31:0] Data_out
);

  wire decoder_1_out0, decoder_1_out1, decoder_1_out2, decoder_1_out3, decoder_2_out0, decoder_2_out1,
       multiplexer_5_out, multiplexer_10_out, multiplexer_11_out, multiplexer_12_out;
  wire [7:0] multiplexer_1_out, multiplexer_2_out, multiplexer_3_out, multiplexer_4_out, multiplexer_6_out,
       multiplexer_7_out, multiplexer_8_out, multiplexer_9_out;

  Decoder #(.select(2), .enable("false")) decoder_1 (
    .out0(decoder_1_out0), .out1(decoder_1_out1), .out2(decoder_1_out2), .out3(decoder_1_out3),
    .sel(Address_2));
  Decoder #(.enable("false")) decoder_2 (.out0(decoder_2_out0), .out1(decoder_2_out1), .sel(Address_2[1]));
  Multiplexer #(.select(2), .width(8), .enable("false")) multiplexer_1 (
    .in0(New_data[7:0]), .in1(New_data[7:0]), .in2(New_data[7:0]), .in3(New_data[7:0]),
    .out(multiplexer_1_out), .sel(Sel));
  Multiplexer #(.select(2), .width(8), .enable("false")) multiplexer_2 (
    .in0(New_data[15:8]), .in1(New_data[15:8]), .in2(New_data[7:0]), .in3(New_data[7:0]),
    .out(multiplexer_2_out), .sel(Sel));
  Multiplexer #(.select(2), .width(8), .enable("false")) multiplexer_3 (
    .in0(New_data[23:16]), .in1(New_data[7:0]), .in2(New_data[7:0]), .in3(New_data[7:0]),
    .out(multiplexer_3_out), .sel(Sel));
  Multiplexer #(.select(2), .width(8), .enable("false")) multiplexer_4 (
    .in0(New_data[31:24]), .in1(New_data[15:8]), .in2(New_data[7:0]), .in3(New_data[7:0]),
    .out(multiplexer_4_out), .sel(Sel));
  Multiplexer #(.select(2), .enable("false")) multiplexer_5 (
    .in0(1'b1), .in1(decoder_2_out0), .in2(decoder_1_out0), .in3(decoder_1_out0), .out(multiplexer_5_out),
    .sel(Sel));
  Multiplexer #(.width(8), .enable("false")) multiplexer_6 (
    .in0(Old_data[7:0]), .in1(multiplexer_1_out), .out(multiplexer_6_out), .sel(multiplexer_5_out));
  Multiplexer #(.width(8), .enable("false")) multiplexer_7 (
    .in0(Old_data[15:8]), .in1(multiplexer_2_out), .out(multiplexer_7_out), .sel(multiplexer_10_out));
  Multiplexer #(.width(8), .enable("false")) multiplexer_8 (
    .in0(Old_data[23:16]), .in1(multiplexer_3_out), .out(multiplexer_8_out), .sel(multiplexer_11_out));
  Multiplexer #(.width(8), .enable("false")) multiplexer_9 (
    .in0(Old_data[31:24]), .in1(multiplexer_4_out), .out(multiplexer_9_out), .sel(multiplexer_12_out));
  Multiplexer #(.select(2), .enable("false")) multiplexer_10 (
    .in0(1'b1), .in1(decoder_2_out0), .in2(decoder_1_out1), .in3(decoder_1_out1), .out(multiplexer_10_out),
    .sel(Sel));
  Multiplexer #(.select(2), .enable("false")) multiplexer_11 (
    .in0(1'b1), .in1(decoder_2_out1), .in2(decoder_1_out2), .in3(decoder_1_out2), .out(multiplexer_11_out),
    .sel(Sel));
  Multiplexer #(.select(2), .enable("false")) multiplexer_12 (
    .in0(1'b1), .in1(decoder_2_out1), .in2(decoder_1_out3), .in3(decoder_1_out3), .out(multiplexer_12_out),
    .sel(Sel));
  assign Data_out = OutputEnable ? {multiplexer_9_out, multiplexer_8_out, multiplexer_7_out, multiplexer_6_out} : 32'bz;  // Controlled_Buffer controlled_buffer_1

  // Notes on the sheet:
  //   Sel = 00 - word
  //   Sel = 01 - halfword
  //   Sel = 1x - byte
  //   Output data composer - replaces part of the old 32-bit memory word with new data based on the two least significant bits of address and the width of new data being written: byte, halfword, or word.
endmodule

module Videoram (
  input  str,
  input  [4:0] Address,
  input  [31:0] Data_In,
  input  ld,
  output [31:0] _0,
  output [31:0] _8,
  output [31:0] _16,
  output [31:0] _24,
  output [31:0] _1,
  output [31:0] _9,
  output [31:0] _17,
  output [31:0] _25,
  output [31:0] _2,
  output [31:0] _10,
  output [31:0] _18,
  output [31:0] _26,
  output [31:0] _3,
  output [31:0] _11,
  output [31:0] _19,
  output [31:0] _27,
  output [31:0] _4,
  output [31:0] _12,
  output [31:0] _20,
  output [31:0] _28,
  output [31:0] _5,
  output [31:0] _13,
  output [31:0] _21,
  output [31:0] _29,
  output [31:0] _6,
  output [31:0] _14,
  output [31:0] _22,
  output [31:0] _30,
  output [31:0] _7,
  output [31:0] _15,
  output [31:0] _23,
  output [31:0] _31,
  output [31:0] Data_Out
);

  wire clock_1_out, clock_2_out, clock_3_out, clock_4_out, clock_5_out, clock_6_out, clock_7_out,
       clock_8_out, clock_9_out, clock_10_out, clock_11_out, clock_12_out, clock_13_out, clock_14_out,
       clock_15_out, clock_16_out, clock_17_out, clock_18_out, clock_19_out, clock_20_out, clock_21_out,
       clock_22_out, clock_23_out, clock_24_out, clock_25_out, clock_26_out, clock_27_out, clock_28_out,
       clock_29_out, clock_30_out, clock_31_out, clock_32_out;
  wire [3:0] decoder_1_out0, decoder_1_out4, decoder_1_out8, decoder_1_out12, decoder_1_out16,
       decoder_1_out20, decoder_1_out24, decoder_1_out28;

  Clock clock_1 (.out(clock_1_out));
  Clock clock_2 (.out(clock_2_out));
  Clock clock_3 (.out(clock_3_out));
  Clock clock_4 (.out(clock_4_out));
  Register #(.width(32)) r0 (.D(Data_In), .en(decoder_1_out0[0]), .Q(_0), .clk(clock_1_out), .clr(1'b0));
  Register #(.width(32)) r1 (.D(Data_In), .en(decoder_1_out0[1]), .Q(_1), .clk(clock_2_out), .clr(1'b0));
  Register #(.width(32)) r2 (.D(Data_In), .en(decoder_1_out0[2]), .Q(_2), .clk(clock_3_out), .clr(1'b0));
  Register #(.width(32)) r3 (.D(Data_In), .en(decoder_1_out0[3]), .Q(_3), .clk(clock_4_out), .clr(1'b0));
  Clock clock_5 (.out(clock_5_out));
  Clock clock_6 (.out(clock_6_out));
  Clock clock_7 (.out(clock_7_out));
  Clock clock_8 (.out(clock_8_out));
  Multiplexer #(.select(5), .width(32)) multiplexer_1 (
    .in0(_0), .in1(_1), .in2(_2), .in3(_3), .in4(_4), .in5(_5), .in6(_6), .in7(_7), .in8(_8), .in9(_9),
    .in10(_10), .in11(_11), .in12(_12), .in13(_13), .in14(_14), .in15(_15), .in16(_16), .in17(_17),
    .in18(_18), .in19(_19), .in20(_20), .in21(_21), .in22(_22), .in23(_23), .in24(_24), .in25(_25),
    .in26(_26), .in27(_27), .in28(_28), .in29(_29), .in30(_30), .in31(_31), .out(Data_Out), .sel(Address),
    .en(ld));
  Register #(.width(32)) r4 (.D(Data_In), .en(decoder_1_out4[0]), .Q(_4), .clk(clock_5_out), .clr(1'b0));
  Register #(.width(32)) r5 (.D(Data_In), .en(decoder_1_out4[1]), .Q(_5), .clk(clock_6_out), .clr(1'b0));
  Register #(.width(32)) r6 (.D(Data_In), .en(decoder_1_out4[2]), .Q(_6), .clk(clock_7_out), .clr(1'b0));
  Register #(.width(32)) r7 (.D(Data_In), .en(decoder_1_out4[3]), .Q(_7), .clk(clock_8_out), .clr(1'b0));
  Decoder #(.select(5), .disabled(0)) decoder_1 (
    .out0(decoder_1_out0[0]), .out1(decoder_1_out0[1]), .out2(decoder_1_out0[2]), .out3(decoder_1_out0[3]),
    .out4(decoder_1_out4[0]), .out5(decoder_1_out4[1]), .out6(decoder_1_out4[2]), .out7(decoder_1_out4[3]),
    .out8(decoder_1_out8[0]), .out9(decoder_1_out8[1]), .out10(decoder_1_out8[2]), .out11(decoder_1_out8[3]),
    .out12(decoder_1_out12[0]), .out13(decoder_1_out12[1]), .out14(decoder_1_out12[2]),
    .out15(decoder_1_out12[3]), .out16(decoder_1_out16[0]), .out17(decoder_1_out16[1]),
    .out18(decoder_1_out16[2]), .out19(decoder_1_out16[3]), .out20(decoder_1_out20[0]),
    .out21(decoder_1_out20[1]), .out22(decoder_1_out20[2]), .out23(decoder_1_out20[3]),
    .out24(decoder_1_out24[0]), .out25(decoder_1_out24[1]), .out26(decoder_1_out24[2]),
    .out27(decoder_1_out24[3]), .out28(decoder_1_out28[0]), .out29(decoder_1_out28[1]),
    .out30(decoder_1_out28[2]), .out31(decoder_1_out28[3]), .sel(Address), .en(str));
  Clock clock_9 (.out(clock_9_out));
  Clock clock_10 (.out(clock_10_out));
  Clock clock_11 (.out(clock_11_out));
  Clock clock_12 (.out(clock_12_out));
  Register #(.width(32)) r8 (.D(Data_In), .en(decoder_1_out8[0]), .Q(_8), .clk(clock_9_out), .clr(1'b0));
  Register #(.width(32)) r9 (.D(Data_In), .en(decoder_1_out8[1]), .Q(_9), .clk(clock_10_out), .clr(1'b0));
  Register #(.width(32)) r10 (.D(Data_In), .en(decoder_1_out8[2]), .Q(_10), .clk(clock_11_out), .clr(1'b0));
  Register #(.width(32)) r11 (.D(Data_In), .en(decoder_1_out8[3]), .Q(_11), .clk(clock_12_out), .clr(1'b0));
  Clock clock_13 (.out(clock_13_out));
  Clock clock_14 (.out(clock_14_out));
  Clock clock_15 (.out(clock_15_out));
  Clock clock_16 (.out(clock_16_out));
  Register #(.width(32)) r12 (.D(Data_In), .en(decoder_1_out12[0]), .Q(_12), .clk(clock_13_out), .clr(1'b0));
  Register #(.width(32)) r13 (.D(Data_In), .en(decoder_1_out12[1]), .Q(_13), .clk(clock_14_out), .clr(1'b0));
  Register #(.width(32)) r14 (.D(Data_In), .en(decoder_1_out12[2]), .Q(_14), .clk(clock_15_out), .clr(1'b0));
  Register #(.width(32)) r15 (.D(Data_In), .en(decoder_1_out12[3]), .Q(_15), .clk(clock_16_out), .clr(1'b0));
  Clock clock_17 (.out(clock_17_out));
  Clock clock_18 (.out(clock_18_out));
  Clock clock_19 (.out(clock_19_out));
  Clock clock_20 (.out(clock_20_out));
  Register #(.width(32)) r16 (.D(Data_In), .en(decoder_1_out16[0]), .Q(_16), .clk(clock_17_out), .clr(1'b0));
  Register #(.width(32)) r17 (.D(Data_In), .en(decoder_1_out16[1]), .Q(_17), .clk(clock_18_out), .clr(1'b0));
  Register #(.width(32)) r18 (.D(Data_In), .en(decoder_1_out16[2]), .Q(_18), .clk(clock_19_out), .clr(1'b0));
  Register #(.width(32)) r19 (.D(Data_In), .en(decoder_1_out16[3]), .Q(_19), .clk(clock_20_out), .clr(1'b0));
  Register #(.width(32)) r20 (.D(Data_In), .en(decoder_1_out20[0]), .Q(_20), .clk(clock_21_out), .clr(1'b0));
  Clock clock_21 (.out(clock_21_out));
  Register #(.width(32)) r21 (.D(Data_In), .en(decoder_1_out20[1]), .Q(_21), .clk(clock_22_out), .clr(1'b0));
  Clock clock_22 (.out(clock_22_out));
  Register #(.width(32)) r22 (.D(Data_In), .en(decoder_1_out20[2]), .Q(_22), .clk(clock_23_out), .clr(1'b0));
  Clock clock_23 (.out(clock_23_out));
  Register #(.width(32)) r23 (.D(Data_In), .en(decoder_1_out20[3]), .Q(_23), .clk(clock_24_out), .clr(1'b0));
  Clock clock_24 (.out(clock_24_out));
  Register #(.width(32)) r24 (.D(Data_In), .en(decoder_1_out24[0]), .Q(_24), .clk(clock_25_out), .clr(1'b0));
  Clock clock_25 (.out(clock_25_out));
  Register #(.width(32)) r25 (.D(Data_In), .en(decoder_1_out24[1]), .Q(_25), .clk(clock_26_out), .clr(1'b0));
  Clock clock_26 (.out(clock_26_out));
  Register #(.width(32)) r26 (.D(Data_In), .en(decoder_1_out24[2]), .Q(_26), .clk(clock_27_out), .clr(1'b0));
  Clock clock_27 (.out(clock_27_out));
  Register #(.width(32)) r27 (.D(Data_In), .en(decoder_1_out24[3]), .Q(_27), .clk(clock_28_out), .clr(1'b0));
  Clock clock_28 (.out(clock_28_out));
  Register #(.width(32)) r28 (.D(Data_In), .en(decoder_1_out28[0]), .Q(_28), .clk(clock_29_out), .clr(1'b0));
  Clock clock_29 (.out(clock_29_out));
  Register #(.width(32)) r29 (.D(Data_In), .en(decoder_1_out28[1]), .Q(_29), .clk(clock_30_out), .clr(1'b0));
  Clock clock_30 (.out(clock_30_out));
  Register #(.width(32)) r30 (.D(Data_In), .en(decoder_1_out28[2]), .Q(_30), .clk(clock_31_out), .clr(1'b0));
  Clock clock_31 (.out(clock_31_out));
  Register #(.width(32)) r31 (.D(Data_In), .en(decoder_1_out28[3]), .Q(_31), .clk(clock_32_out), .clr(1'b0));
  Clock clock_32 (.out(clock_32_out));

  // Other names for the same wires on the sheet: DI[31:0] = Data_In; o0[31:0] = _0; o1[31:0] = _1; o2[31:0] = _2;
  //   o3[31:0] = _3; o4[31:0] = _4; o5[31:0] = _5; o6[31:0] = _6; o7[31:0] = _7; o8[31:0] = _8; o9[31:0] = _9;
  //   o10[31:0] = _10; o11[31:0] = _11; o12[31:0] = _12; o13[31:0] = _13; o14[31:0] = _14; o15[31:0] = _15;
  //   o16[31:0] = _16; o17[31:0] = _17; o18[31:0] = _18; o19[31:0] = _19; o20[31:0] = _20; o21[31:0] = _21;
  //   o22[31:0] = _22; o23[31:0] = _23; o24[31:0] = _24; o25[31:0] = _25; o26[31:0] = _26; o27[31:0] = _27;
  //   o28[31:0] = _28; o29[31:0] = _29; o30[31:0] = _30; o31[31:0] = _31
endmodule
